# Fritzing sketch circuit (saved by Fritzing 0.9.3b)
breadboards: 1

parts:
  Part1 = Arduino MKR1000
  U1 = LIPO-1000mAh [package=lipo-1000]  # not connected
  M1 = DC Motor
  VCC1 = Battery
  R1 = Resistor [tolerance=±5% resistance=10k package=THT]
  R2 = Resistor [tolerance=±5% resistance=10k package=THT]
  D1 = Rectifier Diode [part_number=1N4001 package="300 mil [THT]"]
  D2 = Rectifier Diode [part_number=1N4001 package="300 mil [THT]"]
  D3 = Rectifier Diode [part_number=1N4001 package="300 mil [THT]"]  # not connected
  C1 = Electrolytic Capacitor [capacitance=1µF package="100 mil [THT, electrolytic]"]
  RHT1 = Humidity and Temperature Sensor RHT03
  LED1 = RGB LED (com. cathode, rgb) [package="5 mm [THT]"]
  LED2 = LED - 5mm [color="Red (633nm)" package="5 mm [THT]"]
  R3 = Photocell (LDR) [package=THT]
  Part2 = Soil Moisture Sensor
  Part3 = Soil Moisture Sensor
  R4 = Resistor [tolerance=±5% resistance=10k package=THT]
  R5 = Resistor [tolerance=±5% resistance=220 package=THT]
  R6 = Resistor [tolerance=±5% resistance=220 package=THT]
  R7 = Resistor [tolerance=±5% resistance=220 package=THT]
  R8 = Resistor [tolerance=±5% resistance=220 package=THT]
  R9 = Resistor [tolerance=±5% resistance=220 package=THT]
  T1 = LM35 Temperature Sensor [package="TO92 [THT]"]

nets:
  N1: Part1.A0_DAC0, Part2.SIG
  N2: Part1.A1, Part3.SIG
  N3: Part1.A2, R3.pin_1, R4.Pin_0
  N4: Part1.A3, T1.Vout
  N5: Part1.A4, R2.Pin_0, D2.anode
  N6: Part1.D7, RHT1.Data-signal, R9.Pin_1
  N7: Part1.D9_SCK, LED2.cathode
  N8: Part1.D12_SCL, R7.Pin_0
  N9: Part1.D13_RX, R6.Pin_0
  N10: Part1.14_TX, R5.Pin_0
  N11: M1.pin_1, VCC1.-, R1.Pin_0, C1.-
  N12: M1.pin_2, VCC1.+, D1.anode, C1.+
  N13: R1.Pin_1, D2.cathode
  N14: R2.Pin_1, D1.cathode
  N15: RHT1.Vcc, R8.Pin_0, R9.Pin_0
  N16: LED1.red_anode, R5.Pin_1
  N17: LED1.common_cathode, R6.Pin_1
  GND: LED1.green_anode, Part2.GND, Part3.GND, R4.Pin_1, T1.GND
  N18: LED1.blue_anode, R7.Pin_1
  N19: LED2.anode, R8.Pin_1
  VCC: R3.pin_0, Part2.VCC, Part3.VCC, T1.+Vs

custom parts:
  Arduino MKR1000: MKR1000 is a powerful board that combines the functionality of the Zero and the Wi-Fi Shield. It is the ideal solution for makers wanting to design IoT projects with minimal previous experience in networking
